# Fritzing sketch incubator (saved by Fritzing 0.9.2b)
breadboards: 1

parts:
  Raspberry_Pi1 = Raspberry Pi 2
  R1 = Resistor [tolerance=±5% resistance=4.7k package="2010 [SMD]"]
  U2 = TMP36 [package=to-92-kit]
  U1 = TMP36 [part_number=DS18B20 package=to-92-kit]
  Power_plug2 = Power plug
  MOSFET2 = Basic FET N-Channel [package="TO220 [THT]"]
  LED1 = LED - 3mm [color="Red (633nm)" package="3 mm [THT]"]
  R2 = Resistor [tolerance=±5% resistance=270 package="2010 [SMD]"]
  J1 = Peltier Element [part_number="heating foil"]

nets:
  N1: Raspberry_Pi1.GPIO4, R1.Pin_1, U2.VOUT, U1.VOUT
  N2: Raspberry_Pi1.GPIO21, MOSFET2.gate
  GND: Raspberry_Pi1.GND, U2.GND, Power_plug2.GND, MOSFET2.source
  5V: Raspberry_Pi1.5V, Power_plug2.VCC, LED1.anode, J1.pin1
  N3: R1.Pin_0, U2.VCC
  N4: MOSFET2.drain, R2.Pin_1, J1.pin2
